// Logisim project 32bitALU.circ as structural Verilog: 5 circuits, main circuit Logic Unit
module Logic_Unit (
  input  [1:0] OPCODE,
  input  [31:0] A,
  input  [31:0] B,
  output [31:0] OUTPUT
);

  wire [31:0] and_1_out, nor_1_out, or_1_out, xor_1_out;

  assign and_1_out = A & B;  // AND_Gate and_1, 32 bits wide
  assign or_1_out = A | B;  // OR_Gate or_1, 32 bits wide
  assign nor_1_out = ~(A | B);  // NOR_Gate nor_1, 32 bits wide
  assign xor_1_out = A ^ B;  // XOR_Gate xor_1, 32 bits wide
  Multiplexer #(.select(2), .width(32)) multiplexer_1 (
    .in0(and_1_out), .in1(or_1_out), .in2(nor_1_out), .in3(xor_1_out), .out(OUTPUT), .sel(OPCODE));  // open: en
endmodule

module Shifter (
  input  [31:0] A_LSB_5,
  input  [31:0] B,
  input  [1:0] OPCODE,
  output [31:0] OUTPUT
);

  wire [31:0] shifter_1_out, shifter_2_out, shifter_3_out;

  Shifter_part #(.width(32)) shifter_1 (.in(B), .\dist (A_LSB_5[4:0]), .out(shifter_1_out));
  Shifter_part #(.width(32), .shift("lr")) shifter_2 (.in(B), .\dist (A_LSB_5[4:0]), .out(shifter_2_out));
  Shifter_part #(.width(32), .shift("ar")) shifter_3 (.in(B), .\dist (A_LSB_5[4:0]), .out(shifter_3_out));
  Multiplexer #(.select(2), .width(32)) multiplexer_1 (
    .in0(B), .in1(shifter_1_out), .in2(shifter_2_out), .in3(shifter_3_out), .out(OUTPUT), .sel(OPCODE));  // open: en
endmodule

module Main_ALU (
  input  [1:0] OPCODE,
  input  [31:0] A,
  input  ADDER_OPCODE,
  input  [1:0] OPERATION_OPCODE,
  input  [31:0] B,
  output [31:0] out_6
);

  wire comparator_1_output;
  wire [31:0] adder_1_output, bit_extender_1_out, logic_unit_1_output, nor_1_out, shifter_1_output;

  Shifter shifter_1 (.A_LSB_5(A), .B(B), .OPCODE(OPCODE), .OUTPUT(shifter_1_output));
  Logic_Unit logic_unit_1 (.A(A), .B(B), .OPCODE(OPCODE), .OUTPUT(logic_unit_1_output));
  Comparator comparator_1 (.A(A), .B(B), .OUTPUT(comparator_1_output));
  Adder adder_1 (.A(A), .B(B), .OPCODE(ADDER_OPCODE), .OUTPUT(adder_1_output));
  assign bit_extender_1_out = {{31{1'b0}}, comparator_1_output};  // Bit_Extender bit_extender_1
  Multiplexer #(.select(2), .width(32)) multiplexer_1 (
    .in0(shifter_1_output), .in1(bit_extender_1_out), .in2(adder_1_output), .in3(logic_unit_1_output),
    .out(out_6), .sel(OPERATION_OPCODE));  // open: en
  assign nor_1_out = ~out_6;  // NOR_Gate nor_1, 32 bits wide NOR_Gate

  // Notes on the sheet:
  //   Comparator
  //   Adder
  //   Shifter Operation
  //   Logical Operation Unit
endmodule

module Comparator (
  input  [31:0] A,
  input  [31:0] B,
  output OUTPUT
);

  Comparator_part #(.width(32), .mode("unsigned")) comparator_1 (.a(A), .b(B), .lt(OUTPUT));  // open: gt, eq
endmodule

module Adder (
  input  [31:0] A,
  input  [31:0] B,
  input  OPCODE,
  output [31:0] OUTPUT
);

  wire [31:0] adder_1_out, subtractor_1_out;

  Adder_part #(.width(32)) adder_1 (.a(A), .b(B), .out(adder_1_out));  // open: cin, cout
  Multiplexer #(.width(32)) multiplexer_1 (
    .in0(adder_1_out), .in1(subtractor_1_out), .out(OUTPUT), .sel(OPCODE));  // open: en
  Subtractor #(.width(32)) subtractor_1 (.a(A), .b(B), .out(subtractor_1_out));  // open: bin, bout
endmodule
